# Fritzing sketch schematics (saved by Fritzing 0.9.3b)
breadboards: 1

parts:
  Bauteil2 = Adafruit CCS811
  U3 = NodeMCU V1.0
  R1 = Resistor [tolerance=±5% resistance=4.7k package=THT]
  R2 = Resistor [tolerance=±5% resistance=4.7k package=THT]
  Bauteil4 = BME280 Breakout
  U4 = Molex Picoblade Series Header [part_number=0533980871 package=Picoblade-53398-0871]

nets:
  3.3V: Bauteil2.3.3V, U3.3V3, R2.Pin_1
  GND: Bauteil2.GND, Bauteil2.!WAKE, U3.GND
  N1: Bauteil2.SDA, U3.D2, R2.Pin_0, Bauteil4.SDI/SDA
  N2: Bauteil2.SCL, U3.D1, R1.Pin_1, Bauteil4.SCK/SCL
  N3: U3.D5, U4.5
  N4: U3.D6, U4.4
  N5: U3.RSV#40, R1.Pin_0, U4.1
  N6: U3.RSV#41, U4.2

notes:
  5V  GND
  1: VCC, 2: GND, 4: RXD, 5: TXD
  PMS5003

custom parts:
  NodeMCU V1.0: ESP8266 based NodeMCU
